# Fritzing sketch arduino (saved by Fritzing 0.8.5b)
breadboards: 1

parts:
  U1 = atmega328 [package=dip]
  XTAL1 = Crystal [frequency="16 Mhz" package=THT]
  C1 = Ceramic Capacitor [capacitance=22pF package="100 mil [THT, multilayer]"]
  C2 = Ceramic Capacitor [capacitance=22pF package="100 mil [THT, multilayer]"]
  C3 = Ceramic Capacitor [capacitance=100nF package="100 mil [THT, multilayer]"]
  S1 = Pushbutton [package=THT]
  R1 = Resistor [tolerance=±5% resistance=10k package=THT]
  C4 = Ceramic Capacitor [capacitance=100nF package="100 mil [THT, multilayer]"]
  J2 = female pin header, 2 pins [form="♀ (female)"]
  J3 = female pin header, 2 pins [form="♀ (female)"]
  C5 = Ceramic Capacitor [capacitance=100nF package="100 mil [THT, multilayer]"]
  J1 = rounded female pin header, 2 pins [form="♀ (female rounded)"]
  J7 = AVR ISP 6 Pin [package=2x3]

nets (from the schematic view):
  N1: U1.RESET, S1.leg1, R1.Pin_1, C5.0, J7.5
  N2: U1.D0_(RX), J2.pin1
  N3: U1.D1_(TX), J1.pin2
  5V: U1.VCC, U1.AVCC, C3.0, R1.Pin_0, C4.0, J2.pin2, J7.2
  GND: U1.GND, C1.0, C2.0, C3.1, S1.leg0, C4.1, J3.pin1, J3.pin2, J7.6
  N4: U1.XLAT1, XTAL1.pin_0, C1.1
  N5: U1.XLAT2, XTAL1.pin_1, C2.1
  N6: U1.D11_(PWM), J7.4
  N7: U1.D12, J7.1
  N8: U1.D13, J7.3
  N9: C5.1, J1.pin1
